# Fritzing sketch VaporAutosampler_v1.1 (saved by Fritzing 0.9.3b)
circuit board: 12.5cm x 6.5cm
breadboards: 1

parts:
  24 = Screw terminal - 2 pins [package=THT]
  23 = Screw terminal - 2 pins [package=THT]
  22 = Screw terminal - 2 pins [package=THT]
  21 = Screw terminal - 2 pins [package=THT]
  20 = Screw terminal - 2 pins [package=THT]
  19 = Screw terminal - 2 pins [package=THT]
  18 = Screw terminal - 2 pins [package=THT]
  17 = Screw terminal - 2 pins [package=THT]
  16 = Screw terminal - 2 pins [package=THT]
  15 = Screw terminal - 2 pins [package=THT]
  14 = Screw terminal - 2 pins [package=THT]
  13 = Screw terminal - 2 pins [package=THT]
  12 = Screw terminal - 2 pins [package=THT]
  11 = Screw terminal - 2 pins [package=THT]
  10 = Screw terminal - 2 pins [package=THT]
  9 = Screw terminal - 2 pins [package=THT]
  8 = Screw terminal - 2 pins [package=THT]
  6 = Screw terminal - 2 pins [package=THT]
  5 = Screw terminal - 2 pins [package=THT]
  4 = Screw terminal - 2 pins [package=THT]
  7 = Screw terminal - 2 pins [package=THT]
  3 = Screw terminal - 2 pins [package=THT]
  2 = Screw terminal - 2 pins [package=THT]
  1 = Screw terminal - 2 pins [package=THT]
  U3 = RJ45 Jack [package=rj45-8]
  ULN2803A = ULN2803A [package=THT]
  74HC595 = 74HC595 [package="DIP16 [THT]"]
  LED1 = LED - 3mm [color="Red (633nm)" package="3 mm [THT]"]
  LED2 = LED - 3mm [color="Red (633nm)" package="3 mm [THT]"]
  LED3 = LED - 3mm [color="Red (633nm)" package="3 mm [THT]"]
  LED4 = LED - 3mm [color="Red (633nm)" package="3 mm [THT]"]
  LED5 = LED - 3mm [color="Red (633nm)" package="3 mm [THT]"]
  LED6 = LED - 3mm [color="Red (633nm)" package="3 mm [THT]"]
  LED7 = LED - 3mm [color="Red (633nm)" package="3 mm [THT]"]
  LED8 = LED - 3mm [color="Red (633nm)" package="3 mm [THT]"]
  LED9 = LED - 3mm [color="Red (633nm)" package="3 mm [THT]"]
  LED10 = LED - 3mm [color="Red (633nm)" package="3 mm [THT]"]
  LED11 = LED - 3mm [color="Red (633nm)" package="3 mm [THT]"]
  LED12 = LED - 3mm [color="Red (633nm)" package="3 mm [THT]"]
  LED13 = LED - 3mm [color="Red (633nm)" package="3 mm [THT]"]
  LED14 = LED - 3mm [color="Red (633nm)" package="3 mm [THT]"]
  LED15 = LED - 3mm [color="Red (633nm)" package="3 mm [THT]"]
  LED16 = LED - 3mm [color="Red (633nm)" package="3 mm [THT]"]
  LED17 = LED - 3mm [color="Red (633nm)" package="3 mm [THT]"]
  LED18 = LED - 3mm [color="Red (633nm)" package="3 mm [THT]"]
  LED19 = LED - 3mm [color="Red (633nm)" package="3 mm [THT]"]
  LED20 = LED - 3mm [color="Red (633nm)" package="3 mm [THT]"]
  LED21 = LED - 3mm [color="Red (633nm)" package="3 mm [THT]"]
  LED22 = LED - 3mm [color="Red (633nm)" package="3 mm [THT]"]
  LED23 = LED - 3mm [color="Red (633nm)" package="3 mm [THT]"]
  LED24 = LED - 3mm [color="Red (633nm)" package="3 mm [THT]"]
  ULN2803A_2 = ULN2803A [package=THT]
  ULN2803A1 = ULN2803A [package=THT]
  74HC595_2 = 74HC595 [package="DIP16 [THT]"]
  74HC595_3 = 74HC595 [package="DIP16 [THT]"]
  U5 = RJ45 Jack [package=rj45-8]
  J1 = female pin header, 15 pins [form="♀ (female)"]
  J3 = female pin header, 15 pins [form="♀ (female)"]
  J4 = Power Jack [package=power_jack_pth_lock]
  VCC_B_A_GND = female pin header, 4 pins [form="♀ (female)"]
  DI_DE_RE_RO = female pin header, 4 pins [form="♀ (female)"]
  SW5 = DIP Switch 4 Position [package=dipswitch-04]
  3_3k11 = Resistor [tolerance=±5% resistance=3.3k package=THT]
  3_3k12 = Resistor [tolerance=±5% resistance=6.8k package=THT]
  3_3k13 = Resistor [tolerance=±5% resistance=15k package=THT]
  3_3k14 = Resistor [tolerance=±5% resistance=33k package=THT]
  3_3k15 = Resistor [tolerance=±5% resistance=68k package=THT]
  IC1 = Voltage Regulator [package=to220-igo]
  C1 = Ceramic Capacitor [capacitance=100nF package="100 mil [THT, multilayer]"]
  C2 = Ceramic Capacitor [capacitance=100nF package="100 mil [THT, multilayer]"]
  IC2 = Voltage Regulator [package=to220-igo]
  C4 = Ceramic Capacitor [capacitance=100nF package="100 mil [THT, multilayer]"]
  C5 = Ceramic Capacitor [capacitance=100nF package="100 mil [THT, multilayer]"]
  GND_5V_SCK_SDA = female pin header, 4 pins [form="♀ (female)"]
  J5 = female pin header, 2 pins [form="♀ (female)"]
  U6 = mystery part, 3 pins [chip_label=?]
  J6 = female pin header, 3 pins [form="♀ (female)"]
  J7 = female pin header, 3 pins [form="♀ (female)"]
  R2 = Resistor [tolerance=±5% resistance=430 package=THT]
  J8 = double row female pin header, 10 pins [form="♀ (female)"]
  IN+ = female pin header, 1 pin [form="♀ (female)"]
  IN- = female pin header, 1 pin [form="♀ (female)"]
  OUT+ = female pin header, 1 pin [form="♀ (female)"]
  OUT- = female pin header, 1 pin [form="♀ (female)"]
  R3 = Resistor [tolerance=±5% resistance=4.7k package=THT]
  J9 = female pin header, 2 pins [form="♀ (female)"]
  R4 = Resistor [tolerance=±5% resistance=20k package=THT]
  C8 = Ceramic Capacitor [capacitance=100nF package="100 mil [THT, multilayer]"]
  C9 = Ceramic Capacitor [capacitance=100nF package="100 mil [THT, multilayer]"]
  C10 = Ceramic Capacitor [capacitance=100nF package="100 mil [THT, multilayer]"]

nets:
  N1: 24.pin1, 23.pin1, 22.pin1, 21.pin1, 20.pin1, 19.pin1, 18.pin1, 17.pin1, 16.pin1, 15.pin1, 14.pin1, 13.pin1, 12.pin1, 11.pin1, 10.pin1, 9.pin1, 8.pin1, 6.pin1, 5.pin1, 4.pin1, 7.pin1, 3.pin1, 2.pin1, 1.pin1, ULN2803A.COM_-_Common, ULN2803A_2.COM_-_Common, ULN2803A1.COM_-_Common, IC1.OUT, C2.1, R2.Pin_1, J8.pin2, OUT+.pin1
  N2: 24.pin2, ULN2803A.Out_8, LED1.cathode
  N3: 23.pin2, ULN2803A.Out_7, LED7.cathode
  N4: 22.pin2, ULN2803A.Out_6, LED2.cathode
  N5: 21.pin2, ULN2803A.Out_5, LED3.cathode
  N6: 20.pin2, ULN2803A.Out_4, LED4.cathode
  N7: 19.pin2, ULN2803A.Out_3, LED5.cathode
  N8: 18.pin2, ULN2803A.Out_2, LED6.cathode
  N9: 17.pin2, ULN2803A.Out_1, LED8.cathode
  N10: 16.pin2, LED10.cathode, ULN2803A_2.Out_8
  N11: 15.pin2, LED9.cathode, ULN2803A_2.Out_7
  N12: 14.pin2, LED11.cathode, ULN2803A_2.Out_6
  N13: 13.pin2, LED12.cathode, ULN2803A_2.Out_5
  N14: 12.pin2, LED13.cathode, ULN2803A_2.Out_4
  N15: 11.pin2, LED14.cathode, ULN2803A_2.Out_3
  N16: 10.pin2, LED21.cathode, ULN2803A_2.Out_2
  N17: 9.pin2, LED22.cathode, ULN2803A_2.Out_1
  N18: 8.pin2, LED23.cathode, ULN2803A1.Out_8
  N19: 6.pin2, LED15.cathode, ULN2803A1.Out_6
  N20: 5.pin2, LED16.cathode, ULN2803A1.Out_5
  N21: 4.pin2, LED17.cathode, ULN2803A1.Out_4
  N22: 7.pin2, LED24.cathode, ULN2803A1.Out_7
  N23: 3.pin2, LED18.cathode, ULN2803A1.Out_3
  N24: 2.pin2, LED19.cathode, ULN2803A1.Out_2
  N25: 1.pin2, LED20.cathode, ULN2803A1.Out_1
  N26: U3.1, U5.1, VCC_B_A_GND.pin2
  N27: U3.2, U5.2, VCC_B_A_GND.pin3
  GND: U3.3, U3.5, U3.7, ULN2803A.0V, 74HC595.GND, ULN2803A_2.0V, ULN2803A1.0V, 74HC595_2.GND, 74HC595_3.GND, U5.3, U5.5, U5.7, J1.pin14, J4.GND, J4.GNDBREAK, VCC_B_A_GND.pin4, 3_3k11.Pin_1, IC1.GND, C1.1, C2.0, IC2.GND, C4.0, C5.0, GND_5V_SCK_SDA.pin1, U6.pin1, J8.pin3, IN-.pin1, OUT-.pin1, C8.0, C9.0, C10.0
  N28: U3.4, U3.6, U3.8, U5.4, U5.6, U5.8, J4.PWR, IC1.IN, C1.0, IC2.IN, C5.1, IN+.pin1, J9.pin1
  N29: ULN2803A.In_1, 74HC595.Q7
  N30: ULN2803A.In_2, 74HC595.Q6
  N31: ULN2803A.In_3, 74HC595.Q5
  N32: ULN2803A.In_4, 74HC595.Q4
  N33: ULN2803A.In_5, 74HC595.Q3
  N34: ULN2803A.In_6, 74HC595.Q2
  N35: ULN2803A.In_7, 74HC595.Q1
  N36: ULN2803A.In_8, 74HC595.Q0
  N37: 74HC595.Q7', 74HC595_2.DS
  VCC: 74HC595.MR, 74HC595.VCC, 74HC595_2.MR, 74HC595_2.VCC, 74HC595_3.MR, 74HC595_3.VCC, J1.pin12, VCC_B_A_GND.pin1, SW5.5, SW5.6, SW5.7, SW5.8, IC2.OUT, C4.1, GND_5V_SCK_SDA.pin2, U6.pin3, J8.pin4, R3.Pin_0, R4.Pin_1, C8.1, C9.1, C10.1
  N38: 74HC595.SH_CP, 74HC595_2.SH_CP, 74HC595_3.SH_CP, J3.pin4
  N39: 74HC595.ST_CP, 74HC595_2.ST_CP, 74HC595_3.ST_CP, J3.pin5
  N40: 74HC595.OE, 74HC595_2.OE, 74HC595_3.OE, J3.pin6, R4.Pin_0
  N41: 74HC595.DS, J3.pin11
  N42: LED1.anode, LED2.anode, LED3.anode, LED4.anode, LED5.anode, LED6.anode, LED7.anode, LED8.anode, LED9.anode, LED10.anode, LED11.anode, LED12.anode, LED13.anode, LED14.anode, LED15.anode, LED16.anode, LED17.anode, LED18.anode, LED19.anode, LED20.anode, LED21.anode, LED22.anode, LED23.anode, LED24.anode, R2.Pin_0
  N43: ULN2803A_2.In_1, 74HC595_2.Q7
  N44: ULN2803A_2.In_2, 74HC595_2.Q6
  N45: ULN2803A_2.In_3, 74HC595_2.Q5
  N46: ULN2803A_2.In_4, 74HC595_2.Q4
  N47: ULN2803A_2.In_5, 74HC595_2.Q3
  N48: ULN2803A_2.In_6, 74HC595_2.Q2
  N49: ULN2803A_2.In_7, 74HC595_2.Q1
  N50: ULN2803A_2.In_8, 74HC595_2.Q0
  N51: ULN2803A1.In_1, 74HC595_3.Q7
  N52: ULN2803A1.In_2, 74HC595_3.Q6
  N53: ULN2803A1.In_3, 74HC595_3.Q5
  N54: ULN2803A1.In_4, 74HC595_3.Q4
  N55: ULN2803A1.In_5, 74HC595_3.Q3
  N56: ULN2803A1.In_6, 74HC595_3.Q2
  N57: ULN2803A1.In_7, 74HC595_3.Q1
  N58: ULN2803A1.In_8, 74HC595_3.Q0
  N59: 74HC595_2.Q7', 74HC595_3.DS
  N60: J1.pin4, DI_DE_RE_RO.pin2, DI_DE_RE_RO.pin3
  N61: J1.pin5, J8.pin8
  N62: J1.pin6, J8.pin7
  N63: J1.pin7, J8.pin6
  N64: J1.pin8, GND_5V_SCK_SDA.pin4, J5.pin1
  N65: J1.pin9, GND_5V_SCK_SDA.pin3, J5.pin2
  N66: J1.pin10, J8.pin5
  N67: J1.pin11, 3_3k11.Pin_0, 3_3k12.Pin_0, 3_3k13.Pin_0, 3_3k14.Pin_0, 3_3k15.Pin_0
  N68: J1.pin15, J9.pin2
  N69: J3.pin3, J7.pin1
  N70: J3.pin7, J8.pin10
  N71: J3.pin8, J8.pin9
  N72: J3.pin9, J6.pin1
  N73: J3.pin10, U6.pin2, R3.Pin_1
  N74: J3.pin14, J6.pin3
  N75: J3.pin15, J7.pin3
  N76: DI_DE_RE_RO.pin1, J7.pin2
  N77: DI_DE_RE_RO.pin4, J6.pin2
  N78: SW5.1, 3_3k12.Pin_1
  N79: SW5.2, 3_3k13.Pin_1
  N80: SW5.3, 3_3k14.Pin_1
  N81: SW5.4, 3_3k15.Pin_1

notes:
  RAW GND RST VCC  A3  A2  A1  A0 D13 D12 D11 D10
  VIN
  TX0 RX1 RST GND  2   3   4   5   6   7   8   9
  VIN GND RST  5V  A7  A6  A5  A4  A3  A2  A1  A0 REF  3V D13
  TX1 RX0 RST GND D2  D3  D4  D5  D6  D7  D8  D9  D10 D11 D12
  GND
  5V
  12V
  A5         A4
  RX
  TX
  STX
  SRX
  RO
  DI
  D6
  Ax
  X2
  X3
  D5
  DS18B20
  X1
  ST_CP
  SH_CP
  OE
  MR
  DS
  Q7'
  TDAT
  MAX485 module
  VaporAutosampler_v1.1
  https://github.com/stseeger/VapAuSa
  ----
  master
  slave
  LM2596
  HW-411
  VCC B A GND
  Arduino Nano/ProMini
  supply
  Arduino
  NC
